// Logisim project 3-8 дешифратор на и-не.circ as structural Verilog: 1 circuit, main circuit main
module main (
  input  in_1,
  input  in_2,
  input  in_3
);

  wire decoder_1_out0, decoder_1_out1, decoder_1_out2, decoder_1_out3, decoder_1_out4, decoder_1_out5,
       decoder_1_out6, decoder_1_out7, nand_1_out, nand_2_out, nand_3_out, nand_4_out, nand_5_out,
       nand_6_out, nand_7_out, nand_8_out, nand_9_out, nand_10_out, nand_11_out, nand_12_out, nand_13_out,
       nand_14_out, nand_15_out, nand_16_out, nand_17_out, nand_18_out, nand_19_out;

  nand nand_1 (nand_1_out, in_2, in_2);
  nand nand_2 (nand_2_out, in_1, in_1);
  nand nand_3 (nand_3_out, in_3, in_3);
  nand nand_4 (nand_4_out, 1'b1, nand_2_out, nand_1_out, nand_3_out);
  nand nand_5 (nand_5_out, 1'b1, nand_1_out, nand_2_out, in_3);
  nand nand_6 (nand_6_out, 1'b1, nand_3_out, nand_2_out, in_2);
  nand nand_7 (nand_7_out, 1'b1, nand_2_out, in_3, in_2);
  nand nand_8 (nand_8_out, 1'b1, nand_3_out, nand_1_out, in_1);
  nand nand_9 (nand_9_out, 1'b1, nand_1_out, in_3, in_1);
  nand nand_10 (nand_10_out, 1'b1, nand_3_out, in_2, in_1);
  nand nand_11 (nand_11_out, 1'b1, in_3, in_2, in_1);
  nand nand_12 (nand_12_out, nand_4_out, nand_4_out);
  nand nand_13 (nand_13_out, nand_5_out, nand_5_out);
  nand nand_14 (nand_14_out, nand_6_out, nand_6_out);
  nand nand_15 (nand_15_out, nand_7_out, nand_7_out);
  nand nand_16 (nand_16_out, nand_8_out, nand_8_out);
  nand nand_17 (nand_17_out, nand_9_out, nand_9_out);
  nand nand_18 (nand_18_out, nand_10_out, nand_10_out);
  nand nand_19 (nand_19_out, nand_11_out, nand_11_out);
  Decoder #(.select(3)) decoder_1 (
    .out0(decoder_1_out0), .out1(decoder_1_out1), .out2(decoder_1_out2), .out3(decoder_1_out3),
    .out4(decoder_1_out4), .out5(decoder_1_out5), .out6(decoder_1_out6), .out7(decoder_1_out7),
    .sel({in_1, in_2, in_3}), .en(1'b1));
endmodule
