// Logisim project 3-8 дешифратор на или-не.circ as structural Verilog: 1 circuit, main circuit main
module main (
);

  wire decoder_1_out0, decoder_1_out1, decoder_1_out2, decoder_1_out3, decoder_1_out4, decoder_1_out5,
       decoder_1_out6, decoder_1_out7, nor_1_out, nor_2_out, nor_3_out, nor_4_out, nor_5_out, nor_6_out,
       nor_7_out, nor_8_out, nor_9_out, nor_10_out, nor_11_out, nor_12_out, nor_13_out, nor_14_out,
       nor_15_out, nor_16_out, nor_17_out, nor_18_out, nor_19_out, nor_20_out, nor_21_out, nor_22_out,
       nor_23_out, nor_24_out, nor_25_out, nor_26_out, nor_27_out, nor_28_out;

  nor nor_1 (nor_1_out, 1'b0, 1'b0);
  nor nor_2 (nor_2_out, 1'b1, 1'b1);
  nor nor_3 (nor_3_out, 1'b1, 1'b1);
  nor nor_4 (nor_4_out, 1'b1, 1'b0, 1'b1);
  nor nor_5 (nor_5_out, nor_2_out, 1'b0, 1'b1);
  nor nor_6 (nor_6_out, 1'b1, nor_1_out, 1'b1);
  nor nor_7 (nor_7_out, nor_2_out, nor_1_out, 1'b1);
  nor nor_8 (nor_8_out, 1'b1, 1'b0, nor_3_out);
  nor nor_9 (nor_9_out, nor_2_out, 1'b0, nor_3_out);
  nor nor_10 (nor_10_out, 1'b1, nor_1_out, nor_3_out);
  nor nor_11 (nor_11_out, nor_2_out, nor_1_out, nor_3_out);
  nor nor_12 (nor_12_out, 1'b1, 1'b1);
  nor nor_13 (nor_13_out, nor_12_out, nor_4_out);
  nor nor_14 (nor_14_out, nor_12_out, nor_5_out);
  nor nor_15 (nor_15_out, nor_12_out, nor_6_out);
  nor nor_16 (nor_16_out, nor_12_out, nor_7_out);
  nor nor_17 (nor_17_out, nor_12_out, nor_8_out);
  nor nor_18 (nor_18_out, nor_12_out, nor_9_out);
  nor nor_19 (nor_19_out, nor_12_out, nor_10_out);
  nor nor_20 (nor_20_out, nor_12_out, nor_11_out);
  Decoder #(.select(3)) decoder_1 (
    .out0(decoder_1_out0), .out1(decoder_1_out1), .out2(decoder_1_out2), .out3(decoder_1_out3),
    .out4(decoder_1_out4), .out5(decoder_1_out5), .out6(decoder_1_out6), .out7(decoder_1_out7), .sel(3'b101),
    .en(1'b1));
  nor nor_21 (nor_21_out, nor_13_out, nor_13_out);
  nor nor_22 (nor_22_out, nor_14_out, nor_14_out);
  nor nor_23 (nor_23_out, nor_15_out, nor_15_out);
  nor nor_24 (nor_24_out, nor_16_out, nor_16_out);
  nor nor_25 (nor_25_out, nor_17_out, nor_17_out);
  nor nor_26 (nor_26_out, nor_18_out, nor_18_out);
  nor nor_27 (nor_27_out, nor_19_out, nor_19_out);
  nor nor_28 (nor_28_out, nor_20_out, nor_20_out);
endmodule
